// Logisim project cpu.circ as structural Verilog: 4 circuits, main circuit main
module main (
  input  [31:0] INSTRUCTION,
  input  CLOCK,
  output [31:0] FETCH_ADDRESS,
  output [31:0] ra,
  output [31:0] sp,
  output [31:0] t0,
  output [31:0] t1,
  output [31:0] t2,
  output [31:0] s0,
  output [31:0] s1,
  output [31:0] a0
);

  wire ASel, BrEq, BrLt, BrUn, BSel, MemRW, nop, PCSel, remainderhalf, WE;
  wire [1:0] LoadSel, remainderbyte, WB;
  wire [2:0] ImmSel;
  wire [3:0] ALUSel;
  wire [7:0] multiplexer_4_out;
  wire [15:0] multiplexer_5_out;
  wire [31:0] A, adder_1_out, adder_2_out, ALUresult, B, \byte , divider_1_rem, half, Imm, Instruction1,
       Instruction2, Instruction_t, Load, Load1, PC_old, PCold, PROGRAM_COUNTER, read1, read2,
       RegFileWriteData, shifter_2_out;

  Adder #(.width(32)) adder_1 (.a(PROGRAM_COUNTER), .b(32'h4), .out(adder_1_out));  // open: cin, cout
  Register #(.width(32)) PC (.D(adder_1_out), .clk(CLOCK), .Q(PROGRAM_COUNTER));  // open: en, clr
  Register #(.width(32)) register_1 (.D(Instruction1), .clk(CLOCK), .Q(Instruction_t));  // open: en, clr
  Register #(.width(32)) register_2 (.D(PROGRAM_COUNTER), .clk(CLOCK), .Q(PC_old));  // open: en, clr
  Shifter #(.width(32), .shift("lr")) shifter_1 (.in(PROGRAM_COUNTER), .\dist (5'b00010), .out(FETCH_ADDRESS));
  Multiplexer #(.width(32), .enable("false")) multiplexer_1 (
    .in0(Instruction2), .in1(32'h13), .out(Instruction1), .sel(PCSel));
  Comparator #(.width(32)) comparator_1 (.a(INSTRUCTION), .b(32'h13), .eq(nop));  // open: gt, lt
  ImmGen immgen_1 (.STRwoOP(INSTRUCTION[31:7]), .ImmSel(ImmSel), .out_3(Imm));
  regfile_main RegFile (
    .rs2(INSTRUCTION[24:20]), .rd(INSTRUCTION[11:7]), .Read_Data_1(read1), .Read_Data_2(read2), .ra(ra),
    .sp(sp), .t0(t0), .t1(t1), .t2(t2), .s0(s0), .s1(s1), .a0(a0), .rs1(INSTRUCTION[19:15]),
    .Write_Data(RegFileWriteData), .RegWEn(WE), .clk(CLOCK));  // open: out_16
  Comp comp_1 (.BrUn(BrUn), .A(read1), .B(read2), .BrEq(BrEq), .BrLt(BrLt));
  Control control_1 (
    .BrEq(BrEq), .BrLt(BrLt), .Instr(INSTRUCTION), .PCSel(PCSel), .ImmSel(ImmSel), .ALUSel(ALUSel), .WB(WB),
    .WE(WE), .LoadSel(LoadSel), .BrUn(BrUn), .ASel(ASel), .BSel(BSel), .MemRW(MemRW));
  Multiplexer #(.width(32), .enable("false")) multiplexer_2 (.in0(read1), .in1(PCold), .out(A), .sel(ASel));
  Multiplexer #(.width(32), .enable("false")) multiplexer_3 (.in0(read2), .in1(Imm), .out(B), .sel(BSel));
  Divider #(.width(32)) divider_1 (.a(ALUresult), .b(32'h4), .rem(divider_1_rem));  // open: out, upper
  Bit_Extender #(.in_width(32), .out_width(2)) bit_extender_1 (.in(divider_1_rem), .out(remainderbyte));
  Bit_Extender #(.in_width(32), .out_width(1)) bit_extender_2 (.in(divider_1_rem), .out(remainderhalf));
  Multiplexer #(.select(2), .width(8), .enable("false")) multiplexer_4 (
    .in0(Load[7:0]), .in1(Load[15:8]), .in2(Load[23:16]), .in3(Load[31:24]), .out(multiplexer_4_out),
    .sel(remainderbyte));
  Multiplexer #(.width(16), .enable("false")) multiplexer_5 (
    .in0(Load[15:0]), .in1(Load[31:16]), .out(multiplexer_5_out), .sel(remainderhalf));
  alu Arithmetic_Logic_Unit (
    .A(A), .B(B), .ALUSel(ALUSel), .Result(ALUresult));  // open: in_4, in_5, out_7, out_8, out_9, out_10, out_11, out_12
  assign \byte  = {{24{multiplexer_4_out[7]}}, multiplexer_4_out};  // Bit_Extender bit_extender_3
  assign half = {{16{multiplexer_5_out[15]}}, multiplexer_5_out};  // Bit_Extender bit_extender_4
  Multiplexer #(.select(2), .width(32), .enable("false")) multiplexer_6 (
    .in1(\byte ), .in2(half), .in3(Load), .out(Load1), .sel(LoadSel));  // open: in0
  Shifter #(.width(32), .shift("ar")) shifter_2 (.in(ALUresult), .\dist (5'b00010), .out(shifter_2_out));
  // mem_main DMEM: pin names not known; wires that end beside it: shifter_2_out, read2, MemRW, CLOCK, Load
  Adder #(.width(32)) adder_2 (.a(PC_old), .b(32'h4), .out(adder_2_out));  // open: cin, cout
  Multiplexer #(.select(2), .width(32), .enable("false")) multiplexer_7 (
    .in0(Load1), .in1(ALUresult), .in2(adder_2_out), .out(RegFileWriteData), .sel(WB));  // open: in3

  // Other names for the same wires on the sheet: clk = CLOCK; rd[4:0] = INSTRUCTION[11:7];
  //   STRwoOP[24:0] = INSTRUCTION[31:7]; DataA[4:0] = INSTRUCTION[19:15]; DataB[4:0] = INSTRUCTION[24:20]

  // Notes on the sheet:
  //   Output
  //   Inputs/Outputs from run.circ. DO NOT MOVE THESE.
  //   Inputs
  //   Inputs/Outputs from run.circ. DO NOT MOVE THESE.
endmodule

module Comp (
  input  BrUn,
  input  [31:0] A,
  input  [31:0] B,
  output BrEq,
  output BrLt
);

  wire comparator_1_eq, comparator_1_lt, comparator_2_eq, comparator_2_lt;

  Comparator #(.width(32)) comparator_1 (.a(A), .b(B), .eq(comparator_1_eq), .lt(comparator_1_lt));  // open: gt
  Comparator #(.width(32), .mode("unsigned")) comparator_2 (
    .a(A), .b(B), .eq(comparator_2_eq), .lt(comparator_2_lt));  // open: gt
  Multiplexer #(.enable("false")) multiplexer_1 (.in0(comparator_1_eq), .in1(comparator_2_eq), .out(BrEq), .sel(BrUn));
  Multiplexer #(.enable("false")) multiplexer_2 (.in0(comparator_1_lt), .in1(comparator_2_lt), .out(BrLt), .sel(BrUn));
endmodule

module ImmGen (
  input  [24:0] STRwoOP,
  input  [2:0] ImmSel,
  output [31:0] out_3
);

  wire [31:0] B, I, J, S;

  assign I = {{20{STRwoOP[24]}}, STRwoOP[24:13]};  // Bit_Extender bit_extender_1
  assign S = {{20{STRwoOP[24]}}, {STRwoOP[24:18], STRwoOP[4:0]}};  // Bit_Extender bit_extender_2
  assign B = {{19{STRwoOP[24]}}, {STRwoOP[24], STRwoOP[0], STRwoOP[23:18], STRwoOP[4:1], 1'b0}};  // Bit_Extender bit_extender_3
  assign J = {{11{STRwoOP[24]}}, {STRwoOP[24], STRwoOP[12:5], STRwoOP[13], STRwoOP[23:14], 1'b0}};  // Bit_Extender bit_extender_4
  Multiplexer #(.select(3), .width(32), .enable("false")) multiplexer_1 (
    .in0(I), .in1(S), .in2(B), .in3({STRwoOP[24:5], {12{1'b0}}}), .in4(J), .out(out_3), .sel(ImmSel));  // open: in5, in6, in7

  // Other names for the same wires on the sheet: U[31:12] = STRwoOP[24:5]
endmodule

module Control (
  input  BrEq,
  input  BrLt,
  input  [31:0] Instr,
  output PCSel,
  output [2:0] ImmSel,
  output [3:0] ALUSel,
  output [1:0] WB,
  output WE,
  output [1:0] LoadSel,
  output BrUn,
  output ASel,
  output BSel,
  output MemRW
);

  wire add, and1, and_1_out, and_2_out, and_3_out, and_12_out, and_13_out, and_14_out, and_15_out,
       and_16_out, and_17_out, and_19_out, and_20_out, and_21_out, and_22_out, and_23_out, and_24_out,
       and_27_out, and_28_out, bsel_t, div, func3_0, func3_1, func3_2, func3_3, func3_4, func3_5, func3_6,
       func3_7, func7_00, func7_01, func7_20, mul, mulh, mulhu, not_1_out, not_2_out, op03, op13, op33, op37,
       op63, op67, or1, or_1_out, or_9_out, or_11_out, rem1, sll1, slt1, srai, srl1, sub, xor1;

  // Probe on Instr[31:25]
  Comparator #(.width(7)) comparator_1 (.a(7'b0110011), .b(Instr[6:0]), .eq(op33));  // open: gt, lt
  Comparator #(.width(7)) comparator_2 (.a(7'b0000011), .b(Instr[6:0]), .eq(op03));  // open: gt, lt
  Comparator #(.width(7)) comparator_3 (.a(7'b0010011), .b(Instr[6:0]), .eq(op13));  // open: gt, lt
  Comparator #(.width(7)) comparator_4 (.a(7'b0100011), .b(Instr[6:0]), .eq(MemRW));  // open: gt, lt
  Comparator #(.width(7)) comparator_5 (.a(7'b1100011), .b(Instr[6:0]), .eq(op63));  // open: gt, lt
  Comparator #(.width(7)) comparator_6 (.a(7'b0110111), .b(Instr[6:0]), .eq(op37));  // open: gt, lt
  Comparator #(.width(7)) comparator_7 (.a(7'b1101111), .b(Instr[6:0]), .eq(ImmSel[2]));  // open: gt, lt
  Comparator #(.width(7)) comparator_8 (.a(7'b1100111), .b(Instr[6:0]), .eq(op67));  // open: gt, lt
  Comparator #(.width(3)) comparator_9 (.a(3'b000), .b(Instr[14:12]), .eq(func3_0));  // open: gt, lt
  Comparator #(.width(3)) comparator_10 (.a(3'b001), .b(Instr[14:12]), .eq(func3_1));  // open: gt, lt
  Comparator #(.width(3)) comparator_11 (.a(3'b010), .b(Instr[14:12]), .eq(func3_2));  // open: gt, lt
  Comparator #(.width(3)) comparator_12 (.a(3'b011), .b(Instr[14:12]), .eq(func3_3));  // open: gt, lt
  Comparator #(.width(3)) comparator_13 (.a(3'b100), .b(Instr[14:12]), .eq(func3_4));  // open: gt, lt
  Comparator #(.width(3)) comparator_14 (.a(3'b101), .b(Instr[14:12]), .eq(func3_5));  // open: gt, lt
  Comparator #(.width(3)) comparator_15 (.a(3'b110), .b(Instr[14:12]), .eq(func3_6));  // open: gt, lt
  Comparator #(.width(3)) comparator_16 (.a(3'b111), .b(Instr[14:12]), .eq(func3_7));  // open: gt, lt
  Comparator #(.width(7)) comparator_17 (.a({7{1'b0}}), .b(Instr[31:25]), .eq(func7_00));  // open: gt, lt
  Comparator #(.width(7)) comparator_18 (.a(7'b0000001), .b(Instr[31:25]), .eq(func7_01));  // open: gt, lt
  Comparator #(.width(7)) comparator_19 (.a(7'b0100000), .b(Instr[31:25]), .eq(func7_20));  // open: gt, lt
  and and_1 (and_1_out, op33, func7_00);
  or or_1 (or_1_out, op13, and_1_out);
  and and_2 (and_2_out, op33, func7_00, func3_0);
  and and_3 (and_3_out, op13, func3_0);
  and and_4 (or1, or_1_out, func3_6);
  and and_5 (and1, op13, func3_7);
  and and_6 (and1, op33, func3_7, func7_00);
  and and_7 (sub, op33, func7_20, func3_0);
  and and_8 (mul, op33, func7_01, func3_0);
  and and_9 (rem1, op33, func7_01, func3_7);
  and and_10 (mulhu, op33, func7_01, func3_3);
  or or_2 (add, op03, ImmSel[2], and_2_out, and_3_out, op67, 1'b0);
  and and_11 (bsel_t, op63, op37);
  and and_12 (and_12_out, op03, func3_0);
  and and_13 (and_13_out, op03, func3_2);
  and and_14 (and_14_out, op03, func3_1);
  and and_15 (and_15_out, op03, func3_2);
  or or_3 (LoadSel[0], and_12_out, and_13_out);
  or or_4 (LoadSel[1], and_14_out, and_15_out);
  and and_16 (and_16_out, op33, func7_00, func3_1);
  and and_17 (and_17_out, op13, func7_00, func3_1);
  and and_18 (mulh, op33, func7_01, func3_1);
  and and_19 (and_19_out, op33, func7_00, func3_2);
  and and_20 (and_20_out, op13, func3_2);
  and and_21 (and_21_out, op33, func7_00, func3_4);
  and and_22 (and_22_out, op13, func3_4);
  and and_23 (and_23_out, op33, func7_00, func3_5);
  and and_24 (and_24_out, op13, func7_00, func3_5);
  and and_25 (div, op33, func7_01, func3_5);
  and and_26 (srai, op13, func7_20, func3_5);
  not not_1 (not_1_out, func3_1);
  or or_5 (sll1, and_16_out, and_17_out);
  or or_6 (slt1, and_19_out, and_20_out);
  or or_7 (xor1, and_21_out, and_22_out);
  or or_8 (srl1, and_23_out, and_24_out);
  or or_9 (or_9_out, BrEq, BrLt);
  and and_27 (and_27_out, op63, func3_1, not_2_out);
  not not_2 (not_2_out, BrEq);
  and and_28 (and_28_out, or_9_out, not_1_out, op63);
  or or_10 (PCSel, and_28_out, and_27_out, or_11_out);
  or or_11 (or_11_out, ImmSel[2], op67);
  or or_12 (ImmSel[0], MemRW, op37);
  or or_13 (ImmSel[1], op63, op37);
  or or_14 (ALUSel[0], and1, xor1, srai, slt1, rem1, mulhu, bsel_t);
  or or_15 (ALUSel[1], or1, xor1, sll1, slt1, mul, mulhu, mulh);
  or or_16 (WB[0], op33, op13, op37);
  or or_17 (WB[1], ImmSel[2], op67);
  nor nor_1 (WE, MemRW, op63);
  and and_29 (BrUn, op63, func3_6);
  or or_18 (ASel, op63, ImmSel[2]);
  not not_3 (BSel, op33);
  or or_19 (ALUSel[2], srl1, srai, sll1, slt1, sub, bsel_t, mulh);
  or or_20 (ALUSel[3], div, rem1, mul, mulhu, sub, bsel_t, mulh);

  // Other names for the same wires on the sheet: op6f = ImmSel[2]; opcode[6:0] = Instr[6:0];
  //   func3[2:0] = Instr[14:12]; func7[6:0] = Instr[31:25]; op23 = MemRW
endmodule
