// Logisim project alu.circ as structural Verilog: 2 circuits, main circuit alu
module alu (
  input  [31:0] A,
  input  [31:0] B,
  input  [3:0] ALUSel,
  input  [31:0] in_4,
  input  [31:0] in_5,
  input  [31:0] in_6,
  input  [31:0] in_7,
  input  [31:0] in_8,
  input  [31:0] in_9,
  input  [31:0] in_10,
  input  [31:0] in_11,
  input  [31:0] in_12,
  input  [31:0] in_13,
  input  [3:0] in_14,
  input  [31:0] in_15,
  output [31:0] Result,
  output [31:0] out_17,
  output [31:0] out_18,
  output [31:0] out_19,
  output [4:0] out_20,
  output [31:0] out_21,
  output [31:0] out_22
);

  wire comparator_1_lt, comparator_2_lt, comparator_3_gt, comparator_4_lt, comparator_5_lt, comparator_6_lt,
       comparator_7_eq, xor_3_out;
  wire [4:0] bit_extender_1_out, bit_extender_2_out, bit_extender_3_out, bit_extender_4_out,
       bit_extender_5_out, bit_extender_6_out, bit_extender_11_out;
  wire [31:0] adder_1_out, adder_2_out, adder_3_out, and_1_out, and_2_out, bit_extender_7_out,
       bit_extender_8_out, divider_1_out, divider_2_rem, divider_3_out, divider_4_rem, mulh_1_out_3,
       multiplexer_1_out, multiplexer_4_out, multiplexer_5_out, multiplexer_6_out, multiplier_1_cout,
       multiplier_1_out, multiplier_2_out, multiplier_3_cout, multiplier_4_out, multiplier_5_cout,
       multiplier_6_cout, multiplier_6_out, negator_1_out, negator_2_out, negator_3_out, not_1_out, or_1_out,
       or_2_out, shifter_1_out, shifter_2_out, shifter_3_out, shifter_4_out, shifter_5_out, shifter_6_out,
       subtractor_1_out, subtractor_2_out, subtractor_4_out, xor_1_out, xor_2_out;

  Bit_Extender #(.in_width(32), .out_width(5)) bit_extender_1 (.in(B), .out(bit_extender_1_out));
  Bit_Extender #(.in_width(32), .out_width(5)) bit_extender_2 (.in(B), .out(bit_extender_2_out));
  Bit_Extender #(.in_width(32), .out_width(5)) bit_extender_3 (.in(B), .out(bit_extender_3_out));
  Bit_Extender #(.in_width(32), .out_width(5)) bit_extender_4 (.in(in_15), .out(bit_extender_4_out));
  Bit_Extender #(.in_width(32), .out_width(5)) bit_extender_5 (.in(in_15), .out(bit_extender_5_out));
  Bit_Extender #(.in_width(32), .out_width(5)) bit_extender_6 (.in(in_15), .out(bit_extender_6_out));
  Multiplier #(.width(32)) multiplier_1 (
    .a(in_13), .b(in_15), .out(multiplier_1_out), .cout(multiplier_1_cout));  // open: cin
  Adder #(.width(32)) adder_1 (.a(A), .b(B), .out(adder_1_out));  // open: cin, cout
  assign and_1_out = A & B;  // AND_Gate and_1, 32 bits wide
  assign or_1_out = A | B;  // OR_Gate or_1, 32 bits wide
  assign xor_1_out = A ^ B;  // XOR_Gate xor_1, 32 bits wide
  Shifter #(.width(32), .shift("lr")) shifter_1 (.in(A), .\dist (bit_extender_1_out), .out(shifter_1_out));
  Shifter #(.width(32), .shift("ar")) shifter_2 (.in(A), .\dist (bit_extender_2_out), .out(shifter_2_out));
  Shifter #(.width(32)) shifter_3 (.in(A), .\dist (bit_extender_3_out), .out(shifter_3_out));
  Comparator #(.width(32)) comparator_1 (.a(A), .b(B), .lt(comparator_1_lt));  // open: gt, eq
  Divider #(.width(32)) divider_1 (.a(A), .b(B), .out(divider_1_out));  // open: upper, rem
  Divider #(.width(32)) divider_2 (.a(A), .b(B), .rem(divider_2_rem));  // open: out, upper
  Multiplier #(.width(32)) multiplier_2 (.a(A), .b(B), .out(multiplier_2_out));  // open: cin, cout
  Multiplier #(.width(32)) multiplier_3 (.a(A), .b(B), .cout(multiplier_3_cout));  // open: out, cin
  Subtractor #(.width(32)) subtractor_1 (.a(A), .b(B), .out(subtractor_1_out));  // open: bin, bout
  mulh mulh_1 (.in_1(A), .in_2(B), .out_3(mulh_1_out_3));
  Adder #(.width(32)) adder_2 (.a(in_13), .b(in_15), .out(adder_2_out));  // open: cin, cout
  assign and_2_out = in_13 & in_15;  // AND_Gate and_2, 32 bits wide
  assign or_2_out = in_13 | in_15;  // OR_Gate or_2, 32 bits wide
  assign xor_2_out = in_13 ^ in_15;  // XOR_Gate xor_2, 32 bits wide
  Shifter #(.width(32), .shift("lr")) shifter_4 (.in(in_13), .\dist (bit_extender_4_out), .out(shifter_4_out));
  Shifter #(.width(32), .shift("ar")) shifter_5 (.in(in_13), .\dist (bit_extender_5_out), .out(shifter_5_out));
  Shifter #(.width(32)) shifter_6 (.in(in_13), .\dist (bit_extender_6_out), .out(shifter_6_out));
  Comparator #(.width(32)) comparator_2 (.a(in_13), .b(in_15), .lt(comparator_2_lt));  // open: gt, eq
  Divider #(.width(32)) divider_3 (.a(in_13), .b(in_15), .out(divider_3_out));  // open: upper, rem
  Divider #(.width(32)) divider_4 (.a(in_13), .b(in_15), .rem(divider_4_rem));  // open: out, upper
  Multiplier #(.width(32)) multiplier_4 (.a(in_13), .b(in_15), .out(multiplier_4_out));  // open: cin, cout
  Multiplier #(.width(32)) multiplier_5 (.a(in_13), .b(in_15), .cout(multiplier_5_cout));  // open: out, cin
  Subtractor #(.width(32)) subtractor_2 (.a(in_13), .b(in_15), .out(subtractor_2_out));  // open: bin, bout
  assign not_1_out = ~multiplier_1_cout;  // NOT_Gate not_1, 32 bits wide
  Comparator #(.width(32)) comparator_3 (.a({32{1'b0}}), .b(multiplier_1_out), .gt(comparator_3_gt));  // open: eq, lt
  assign bit_extender_7_out = {{31{1'b0}}, comparator_1_lt};  // Bit_Extender bit_extender_7
  assign bit_extender_8_out = {{31{1'b0}}, comparator_2_lt};  // Bit_Extender bit_extender_8
  Adder #(.width(32)) adder_3 (.a(not_1_out), .b(32'h1), .out(adder_3_out));  // open: cin, cout
  Multiplexer #(.width(32), .enable("false")) multiplexer_1 (
    .in0(multiplier_1_cout), .in1(adder_3_out), .out(multiplexer_1_out), .sel(comparator_3_gt));
  Multiplexer #(.select(4), .width(32), .enable("false")) multiplexer_2 (
    .in0(adder_1_out), .in1(and_1_out), .in2(or_1_out), .in3(xor_1_out), .in4(shifter_1_out),
    .in5(shifter_2_out), .in6(shifter_3_out), .in7(bit_extender_7_out), .in8(divider_1_out),
    .in9(divider_2_rem), .in10(multiplier_2_out), .in11(multiplier_3_cout), .in12(subtractor_1_out),
    .in13(B), .in14(mulh_1_out_3), .out(Result), .sel(ALUSel));  // open: in15
  Multiplexer #(.select(4), .width(32), .enable("false")) multiplexer_3 (
    .in0(adder_2_out), .in1(and_2_out), .in2(or_2_out), .in3(xor_2_out), .in4(shifter_4_out),
    .in5(shifter_5_out), .in6(shifter_6_out), .in7(bit_extender_8_out), .in8(divider_3_out),
    .in9(divider_4_rem), .in10(multiplier_4_out), .in11(multiplier_5_cout), .in12(subtractor_2_out),
    .in13(in_15), .in14(multiplexer_1_out), .out(out_22), .sel(in_14));  // open: in15
  Comparator #(.width(32)) comparator_4 (.a(in_4), .b(in_6), .lt(comparator_4_lt));  // open: gt, eq
  Bit_Extender #(.in_width(32), .out_width(5)) bit_extender_9 (.in(in_10), .out(out_20));
  Negator #(.width(32)) negator_1 (.in(in_11), .out(negator_1_out));
  Comparator #(.width(32)) comparator_5 (.a(in_11), .b({32{1'b0}}), .lt(comparator_5_lt));  // open: gt, eq
  Negator #(.width(32)) negator_2 (.in(in_12), .out(negator_2_out));
  Comparator #(.width(32)) comparator_6 (.a(in_12), .b({32{1'b0}}), .lt(comparator_6_lt));  // open: gt, eq
  assign out_17 = {{31{1'b0}}, comparator_4_lt};  // Bit_Extender bit_extender_10
  Bit_Extender #(.in_width(32), .out_width(5)) bit_extender_11 (.in(in_9), .out(bit_extender_11_out));
  Multiplexer #(.width(32), .enable("false")) multiplexer_4 (
    .in0(in_11), .in1(negator_1_out), .out(multiplexer_4_out), .sel(comparator_5_lt));
  Multiplexer #(.width(32), .enable("false")) multiplexer_5 (
    .in0(in_12), .in1(negator_2_out), .out(multiplexer_5_out), .sel(comparator_6_lt));
  Shifter #(.width(32), .shift("lr")) shifter_7 (.in(in_8), .\dist (bit_extender_11_out), .out(out_19));
  Multiplier #(.width(32)) multiplier_6 (
    .a(multiplexer_4_out), .b(multiplexer_5_out), .out(multiplier_6_out), .cout(multiplier_6_cout));  // open: cin
  xor xor_3 (xor_3_out, comparator_5_lt, comparator_6_lt);
  Comparator #(.width(32)) comparator_7 (.a(multiplier_6_out), .b({32{1'b0}}), .eq(comparator_7_eq));  // open: gt, lt
  Negator #(.width(32)) negator_3 (.in(multiplier_6_cout), .out(negator_3_out));
  Subtractor #(.width(32)) subtractor_3 (.a(in_5), .b(in_7), .out(out_18));  // open: bin, bout
  Subtractor #(.width(32)) subtractor_4 (.a(negator_3_out), .b(32'h1), .out(subtractor_4_out));  // open: bin, bout
  Multiplexer #(.width(32), .enable("false")) multiplexer_6 (
    .in0(subtractor_4_out), .in1(negator_3_out), .out(multiplexer_6_out), .sel(comparator_7_eq));
  Multiplexer #(.width(32), .enable("false")) multiplexer_7 (
    .in0(multiplexer_6_out), .in1(multiplier_6_cout), .out(out_21), .sel(xor_3_out));

  // Notes on the sheet:
  //   INPUTS to your circuit
  //   DON'T CHANGE THE LOCATIONS OF THE INPUTS AND OUTPUTS!
  //   OUTPUT from your circuit
endmodule

module mulh (
  input  [31:0] in_1,
  input  [31:0] in_2,
  output [31:0] out_3
);

  wire comparator_1_lt, comparator_2_lt, comparator_3_eq, xnor_1_out;
  wire [31:0] adder_1_out, multiplexer_1_out, multiplexer_2_out, multiplexer_3_out, multiplier_1_cout,
       multiplier_1_out, negator_1_out, negator_2_out, not_1_out;

  Negator #(.width(32)) negator_1 (.in(in_1), .out(negator_1_out));
  Comparator #(.width(32)) comparator_1 (.a(in_1), .b({32{1'b0}}), .lt(comparator_1_lt));  // open: gt, eq
  Negator #(.width(32)) negator_2 (.in(in_2), .out(negator_2_out));
  Comparator #(.width(32)) comparator_2 (.a(in_2), .b({32{1'b0}}), .lt(comparator_2_lt));  // open: gt, eq
  Multiplexer #(.width(32), .enable("false")) multiplexer_1 (
    .in0(in_1), .in1(negator_1_out), .out(multiplexer_1_out), .sel(comparator_1_lt));
  Multiplexer #(.width(32), .enable("false")) multiplexer_2 (
    .in0(in_2), .in1(negator_2_out), .out(multiplexer_2_out), .sel(comparator_2_lt));
  Multiplier #(.width(32)) multiplier_1 (
    .a(multiplexer_1_out), .b(multiplexer_2_out), .out(multiplier_1_out), .cout(multiplier_1_cout));  // open: cin
  xnor xnor_1 (xnor_1_out, comparator_1_lt, comparator_2_lt);
  assign not_1_out = ~multiplier_1_cout;  // NOT_Gate not_1, 32 bits wide
  Comparator #(.width(32)) comparator_3 (.a(multiplier_1_out), .b({32{1'b0}}), .eq(comparator_3_eq));  // open: gt, lt
  Adder #(.width(32)) adder_1 (.a(not_1_out), .b(32'h1), .out(adder_1_out));  // open: cin, cout
  Multiplexer #(.width(32), .enable("false")) multiplexer_3 (
    .in0(not_1_out), .in1(adder_1_out), .out(multiplexer_3_out), .sel(comparator_3_eq));
  Multiplexer #(.width(32), .enable("false")) multiplexer_4 (
    .in0(multiplexer_3_out), .in1(multiplier_1_cout), .out(out_3), .sel(xnor_1_out));
endmodule
