// Logisim project cpu.circ as structural Verilog: 4 circuits, main circuit main
module main (
  input  [31:0] INSTRUCTION,
  input  CLOCK,
  output [31:0] FETCH_ADDRESS,
  output [31:0] ra,
  output [31:0] sp,
  output [31:0] t0,
  output [31:0] t1,
  output [31:0] t2,
  output [31:0] s0,
  output [31:0] s1,
  output [31:0] a0
);

  wire and_1_out, ASel, BrEq, BrLt, BrUn, BSel, comparator_1_eq, HalfSel, lwcSel, MemRW, multiplexer_7_out,
       multiplexer_13_out, PCSel, popSel, pushSel, WE;
  wire [1:0] ByteSel, divider_2_out, LoadSel, WB;
  wire [2:0] ImmSel;
  wire [3:0] ALUSel;
  wire [4:0] DataA, DataB, multiplexer_6_out, rd;
  wire [7:0] multiplexer_11_out;
  wire [15:0] multiplexer_12_out;
  wire [31:0] adder_1_out, adder_2_out, ALUresult, bit_extender_1_out, Byte, divider_1_rem, Half, Imm,
       immgen_1_out_3, Instr_post, Load, multiplexer_1_out, multiplexer_2_out, multiplexer_9_out,
       multiplexer_10_out, multiplexer_14_out, multiplexer_16_out, PC_old, PROGRAM_COUNTER, read1, read2,
       RegFileWriteData, subtractor_1_out, subtractor_2_out, Word;

  Adder #(.width(32)) adder_1 (.a(PROGRAM_COUNTER), .b(32'h4), .out(adder_1_out));  // open: cin, cout
  Register #(.width(32)) PC_pipe (.D(PROGRAM_COUNTER), .clk(CLOCK), .Q(PC_old));  // open: en, clr
  Shifter #(.width(32), .shift("lr")) shifter_1 (.in(PROGRAM_COUNTER), .\dist (5'b00010), .out(FETCH_ADDRESS));
  Multiplexer #(.width(32), .enable("false")) multiplexer_1 (
    .in0(adder_1_out), .in1(ALUresult), .out(multiplexer_1_out), .sel(PCSel));
  Register #(.width(32)) Instr_pipe (.D(multiplexer_2_out), .clk(CLOCK), .Q(Instr_post));  // open: en, clr
  Multiplexer #(.width(32), .enable("false")) multiplexer_2 (
    .in0(INSTRUCTION), .in1(32'h13), .out(multiplexer_2_out), .sel(PCSel));
  Register #(.width(32)) PC (.D(multiplexer_1_out), .clk(CLOCK), .Q(PROGRAM_COUNTER));  // open: en, clr
  Multiplexer #(.width(5), .enable("false")) multiplexer_3 (
    .in0(Instr_post[24:20]), .in1(5'b00010), .out(DataB), .sel(popSel));
  Multiplexer #(.width(5), .enable("false")) multiplexer_4 (
    .in0(Instr_post[11:7]), .in1(5'b00010), .out(rd), .sel(popSel));
  Multiplexer #(.width(5), .enable("false")) multiplexer_5 (
    .in0(Instr_post[19:15]), .in1(5'b00010), .out(DataA), .sel(popSel));
  Comparator #(.width(32)) comparator_1 (.a(read2), .b({32{1'b0}}), .eq(comparator_1_eq));  // open: gt, lt
  Multiplexer #(.width(5), .enable("false")) multiplexer_6 (
    .in0(rd), .in1(5'b00010), .out(multiplexer_6_out), .sel(pushSel));
  Multiplexer #(.enable("false")) multiplexer_7 (.in0(WE), .in1(1'b0), .out(multiplexer_7_out), .sel(and_1_out));
  and and_1 (and_1_out, comparator_1_eq, lwcSel);
  Control control_1 (
    .BrEq(BrEq), .BrLt(BrLt), .Instr(Instr_post), .PCSel(PCSel), .ImmSel(ImmSel), .ALUSel(ALUSel),
    .lwcSel(lwcSel), .pushsel(pushSel), .WB(WB), .popSel(popSel), .WE(WE), .BrUn(BrUn), .ASel(ASel),
    .BSel(BSel), .LoadSel(LoadSel), .MemRW(MemRW));
  ImmGen immgen_1 (.STRwoOP(Instr_post[31:7]), .ImmSel(ImmSel), .out_3(immgen_1_out_3));
  assign bit_extender_1_out = {{25{Instr_post[31]}}, Instr_post[31:25]};  // Bit_Extender bit_extender_1
  regfile_main RegFile (
    .rs2(DataB), .rd(multiplexer_6_out), .Read_Data_1(read1), .Read_Data_2(read2), .ra(ra), .sp(sp), .t0(t0),
    .t1(t1), .t2(t2), .s0(s0), .s1(s1), .a0(a0), .rs1(DataA), .Write_Data(RegFileWriteData),
    .RegWEn(multiplexer_7_out), .clk(CLOCK));  // open: out_16
  Multiplexer #(.width(32), .enable("false")) multiplexer_8 (
    .in0(immgen_1_out_3), .in1(bit_extender_1_out), .out(Imm), .sel(lwcSel));
  Multiplexer #(.width(32), .enable("false")) multiplexer_9 (
    .in0(read1), .in1(PC_old), .out(multiplexer_9_out), .sel(ASel));
  Multiplexer #(.width(32), .enable("false")) multiplexer_10 (
    .in0(read2), .in1(Imm), .out(multiplexer_10_out), .sel(BSel));
  Divider #(.width(32)) divider_1 (.a(ALUresult), .b(32'h4), .rem(divider_1_rem));  // open: out, upper
  Bit_Extender #(.in_width(32), .out_width(2)) bit_extender_2 (.in(divider_1_rem), .out(ByteSel));
  Comp comp_1 (.BrUn(BrUn), .A(read1), .B(read2), .BrEq(BrEq), .BrLt(BrLt));
  Divider #(.width(2)) divider_2 (.a(ByteSel), .b(2'b10), .out(divider_2_out));  // open: upper, rem
  Bit_Extender #(.in_width(2), .out_width(1)) bit_extender_3 (.in(divider_2_out), .out(HalfSel));
  alu Arithmetic_Logic_Unit (
    .A(multiplexer_9_out), .B(multiplexer_10_out), .ALUSel(ALUSel), .Result(ALUresult));  // open: in_4, in_5, out_7, out_8, out_9, out_10, out_11, out_12
  Multiplexer #(.select(2), .width(8), .enable("false")) multiplexer_11 (
    .in0(Word[7:0]), .in1(Word[15:8]), .in2(Word[23:16]), .in3(Word[31:24]), .out(multiplexer_11_out),
    .sel(ByteSel));
  Multiplexer #(.width(16), .enable("false")) multiplexer_12 (
    .in0(Word[15:0]), .in1(Word[31:16]), .out(multiplexer_12_out), .sel(HalfSel));
  assign Byte = {{24{multiplexer_11_out[7]}}, multiplexer_11_out};  // Bit_Extender bit_extender_4
  assign Half = {{16{multiplexer_12_out[15]}}, multiplexer_12_out};  // Bit_Extender bit_extender_5
  Subtractor #(.width(32)) subtractor_1 (.a(sp), .b(32'h4), .out(subtractor_1_out));  // open: bin, bout
  Multiplexer #(.enable("false")) multiplexer_13 (.in0(MemRW), .in1(1'b1), .out(multiplexer_13_out), .sel(pushSel));
  Multiplexer #(.width(32), .enable("false")) multiplexer_14 (
    .in0(ALUresult), .in1(subtractor_1_out), .out(multiplexer_14_out), .sel(pushSel));
  Multiplexer #(.select(2), .width(32), .enable("false")) multiplexer_15 (
    .in1(Byte), .in2(Half), .in3(Word), .out(Load), .sel(LoadSel));  // open: in0
  // mem_main DMEM: pin names not known; wires that end beside it: multiplexer_14_out, read2, multiplexer_13_out, CLOCK, Word
  Subtractor #(.width(32)) subtractor_2 (.a(sp), .b(32'h4), .out(subtractor_2_out));  // open: bin, bout
  Multiplexer #(.width(32), .enable("false")) multiplexer_16 (
    .in0(ALUresult), .in1(subtractor_2_out), .out(multiplexer_16_out), .sel(pushSel));
  Adder #(.width(32)) adder_2 (.a(PC_old), .b(32'h4), .out(adder_2_out));  // open: cin, cout
  Multiplexer #(.select(2), .width(32), .enable("false")) multiplexer_17 (
    .in0(Load), .in1(multiplexer_16_out), .in2(adder_2_out), .out(RegFileWriteData), .sel(WB));  // open: in3

  // Other names for the same wires on the sheet: clk = CLOCK; STRwoOP[24:0] = Instr_post[31:7]

  // Notes on the sheet:
  //   Output
  //   Inputs/Outputs from run.circ. DO NOT MOVE THESE.
  //   Inputs
  //   Inputs/Outputs from run.circ. DO NOT MOVE THESE.
endmodule

module Comp (
  input  BrUn,
  input  [31:0] A,
  input  [31:0] B,
  output BrEq,
  output BrLt
);

  wire comparator_1_eq, comparator_1_lt, comparator_2_eq, comparator_2_lt;

  Comparator #(.width(32)) comparator_1 (.a(A), .b(B), .eq(comparator_1_eq), .lt(comparator_1_lt));  // open: gt
  Comparator #(.width(32), .mode("unsigned")) comparator_2 (
    .a(A), .b(B), .eq(comparator_2_eq), .lt(comparator_2_lt));  // open: gt
  Multiplexer #(.enable("false")) multiplexer_1 (.in0(comparator_1_eq), .in1(comparator_2_eq), .out(BrEq), .sel(BrUn));
  Multiplexer #(.enable("false")) multiplexer_2 (.in0(comparator_1_lt), .in1(comparator_2_lt), .out(BrLt), .sel(BrUn));
endmodule

module ImmGen (
  input  [24:0] STRwoOP,
  input  [2:0] ImmSel,
  output [31:0] out_3
);

  wire [31:0] B, I, J, S;

  assign I = {{20{STRwoOP[24]}}, STRwoOP[24:13]};  // Bit_Extender bit_extender_1
  assign S = {{20{STRwoOP[24]}}, {STRwoOP[24:18], STRwoOP[4:0]}};  // Bit_Extender bit_extender_2
  assign B = {{19{STRwoOP[24]}}, {STRwoOP[24], STRwoOP[0], STRwoOP[23:18], STRwoOP[4:1], 1'b0}};  // Bit_Extender bit_extender_3
  assign J = {{11{STRwoOP[24]}}, {STRwoOP[24], STRwoOP[12:5], STRwoOP[13], STRwoOP[23:14], 1'b0}};  // Bit_Extender bit_extender_4
  Multiplexer #(.select(3), .width(32), .enable("false")) multiplexer_1 (
    .in0(I), .in1(S), .in2(B), .in3({STRwoOP[24:5], {12{1'b0}}}), .in4(J), .out(out_3), .sel(ImmSel));  // open: in5, in6, in7

  // Other names for the same wires on the sheet: U[31:12] = STRwoOP[24:5]
endmodule

module Control (
  input  BrEq,
  input  BrLt,
  input  [31:0] Instr,
  output PCSel,
  output [2:0] ImmSel,
  output [3:0] ALUSel,
  output lwcSel,
  output pushsel,
  output [1:0] WB,
  output popSel,
  output WE,
  output BrUn,
  output ASel,
  output BSel,
  output [1:0] LoadSel,
  output MemRW
);

  wire add, and1, and_2_out, and_3_out, and_4_out, and_5_out, and_6_out, and_15_out, and_16_out, and_17_out,
       and_18_out, and_19_out, and_20_out, and_22_out, and_23_out, and_24_out, and_25_out, and_26_out,
       and_27_out, and_29_out, and_30_out, bsel_t, div, Eq_out, func3_0, func3_1, func3_2, func3_3, func3_4,
       func3_5, func3_6, func3_7, func7_00, func7_01, func7_20, Lt_out, mul, mulh, mulhu, Neq_out, op03,
       op3B, op13, op33, op37, op63, op67, or1, or_1_out, or_4_out, or_12_out, rem1, sll1, slt1, srai, srl1,
       sub, xor1;

  Comparator #(.width(7)) comparator_1 (.a(7'b0110011), .b(Instr[6:0]), .eq(op33));  // open: gt, lt
  Comparator #(.width(7)) comparator_2 (.a(7'b0000011), .b(Instr[6:0]), .eq(op03));  // open: gt, lt
  Comparator #(.width(7)) comparator_3 (.a(7'b0010011), .b(Instr[6:0]), .eq(op13));  // open: gt, lt
  Comparator #(.width(7)) comparator_4 (.a(7'b0100011), .b(Instr[6:0]), .eq(MemRW));  // open: gt, lt
  Comparator #(.width(7)) comparator_5 (.a(7'b1100011), .b(Instr[6:0]), .eq(op63));  // open: gt, lt
  Comparator #(.width(7)) comparator_6 (.a(7'b0110111), .b(Instr[6:0]), .eq(op37));  // open: gt, lt
  Comparator #(.width(7)) comparator_7 (.a(7'b1101111), .b(Instr[6:0]), .eq(ImmSel[2]));  // open: gt, lt
  Comparator #(.width(7)) comparator_8 (.a(7'b1100111), .b(Instr[6:0]), .eq(op67));  // open: gt, lt
  Comparator #(.width(7)) comparator_9 (.a(7'b0111011), .b(Instr[6:0]), .eq(op3B));  // open: gt, lt
  Comparator #(.width(3)) comparator_10 (.a(3'b000), .b(Instr[14:12]), .eq(func3_0));  // open: gt, lt
  Comparator #(.width(3)) comparator_11 (.a(3'b001), .b(Instr[14:12]), .eq(func3_1));  // open: gt, lt
  Comparator #(.width(3)) comparator_12 (.a(3'b010), .b(Instr[14:12]), .eq(func3_2));  // open: gt, lt
  Comparator #(.width(3)) comparator_13 (.a(3'b011), .b(Instr[14:12]), .eq(func3_3));  // open: gt, lt
  Comparator #(.width(3)) comparator_14 (.a(3'b100), .b(Instr[14:12]), .eq(func3_4));  // open: gt, lt
  Comparator #(.width(3)) comparator_15 (.a(3'b101), .b(Instr[14:12]), .eq(func3_5));  // open: gt, lt
  Comparator #(.width(3)) comparator_16 (.a(3'b110), .b(Instr[14:12]), .eq(func3_6));  // open: gt, lt
  Comparator #(.width(3)) comparator_17 (.a(3'b111), .b(Instr[14:12]), .eq(func3_7));  // open: gt, lt
  Comparator #(.width(7)) comparator_18 (.a({7{1'b0}}), .b(Instr[31:25]), .eq(func7_00));  // open: gt, lt
  Comparator #(.width(7)) comparator_19 (.a(7'b0000001), .b(Instr[31:25]), .eq(func7_01));  // open: gt, lt
  Comparator #(.width(7)) comparator_20 (.a(7'b0100000), .b(Instr[31:25]), .eq(func7_20));  // open: gt, lt
  and and_1 (lwcSel, op03, func3_7);
  and and_2 (and_2_out, op33, func7_00);
  or or_1 (or_1_out, op13, and_2_out);
  and and_3 (and_3_out, op13, func3_7);
  and and_4 (and_4_out, op33, func3_7, func7_00);
  and and_5 (and_5_out, op33, func7_00, func3_0);
  and and_6 (and_6_out, op13, func3_0);
  and and_7 (popSel, op3B, func3_2);
  and and_8 (or1, or_1_out, func3_6);
  or or_2 (and1, and_3_out, and_4_out);
  and and_9 (sub, op33, func7_20, func3_0);
  and and_10 (mul, op33, func7_01, func3_0);
  and and_11 (rem1, op33, func7_01, func3_7);
  and and_12 (mulhu, op33, func7_01, func3_3);
  or or_3 (add, op03, ImmSel[2], and_5_out, and_6_out, op67, 1'b0);
  and and_13 (bsel_t, op63, op37);
  or or_4 (or_4_out, func3_2, func3_7);
  and and_14 (pushsel, op3B, func3_3);
  and and_15 (and_15_out, op03, func3_0);
  and and_16 (and_16_out, op03, or_4_out);
  and and_17 (and_17_out, op03, func3_1);
  and and_18 (and_18_out, op03, func3_2);
  or or_5 (LoadSel[0], and_15_out, and_16_out);
  or or_6 (LoadSel[1], and_17_out, and_18_out);
  and and_19 (and_19_out, op33, func7_00, func3_1);
  and and_20 (and_20_out, op13, func7_00, func3_1);
  and and_21 (mulh, op33, func7_01, func3_1);
  and and_22 (and_22_out, op33, func7_00, func3_2);
  and and_23 (and_23_out, op13, func3_2);
  and and_24 (and_24_out, op33, func7_00, func3_4);
  and and_25 (and_25_out, op13, func3_4);
  and and_26 (and_26_out, op33, func7_00, func3_5);
  and and_27 (and_27_out, op13, func7_00, func3_5);
  and and_28 (div, op33, func7_01, func3_5);
  and and_29 (and_29_out, op13, func7_20, func3_5);
  and and_30 (and_30_out, op33, func3_5, func7_20);
  or or_7 (srai, and_29_out, and_30_out);
  or or_8 (sll1, and_19_out, and_20_out);
  or or_9 (slt1, and_22_out, and_23_out);
  or or_10 (xor1, and_24_out, and_25_out);
  or or_11 (srl1, and_26_out, and_27_out);
  or or_12 (or_12_out, func3_4, func3_6);
  and Eq (Eq_out, BrEq, op63, func3_0);
  and Lt (Lt_out, BrLt, op63, or_12_out);
  and Neq (Neq_out, op63, func3_1, ~BrEq);  // AND_Gate
  or or_13 (ImmSel[0], MemRW, op37);
  or or_14 (ImmSel[1], op63, op37);
  or or_15 (ALUSel[0], and1, xor1, srai, slt1, rem1, mulhu, bsel_t);
  or or_16 (ALUSel[1], or1, xor1, sll1, slt1, mul, mulhu, mulh);
  or or_17 (WB[0], op33, op3B, op13, op37);
  or or_18 (WB[1], ImmSel[2], op67);
  nor nor_1 (WE, MemRW, op63);
  and and_31 (BrUn, op63, func3_6);
  or or_19 (ASel, op63, ImmSel[2]);
  not not_1 (BSel, op33);
  or or_20 (PCSel, Eq_out, Lt_out, Neq_out, ImmSel[2], op67);
  or or_21 (ALUSel[2], srl1, srai, sll1, slt1, sub, bsel_t, mulh);
  or or_22 (ALUSel[3], div, rem1, mul, mulhu, sub, bsel_t, mulh);

  // Other names for the same wires on the sheet: op6f = ImmSel[2]; opcode[6:0] = Instr[6:0];
  //   func3[2:0] = Instr[14:12]; func7[6:0] = Instr[31:25]; op23 = MemRW
endmodule
