// Logisim project regfile.circ as structural Verilog: 1 circuit, main circuit main
module main (
  input  [4:0] rs1,
  input  [4:0] rs2,
  input  [4:0] rd,
  input  [31:0] Write_Data,
  input  RegWEn,
  input  clk,
  output [31:0] ra,
  output [31:0] sp,
  output [31:0] t0,
  output [31:0] t1,
  output [31:0] t2,
  output [31:0] s0,
  output [31:0] s1,
  output [31:0] a0,
  output [31:0] Read_Data_1,
  output [31:0] out_16,
  output [31:0] Read_Data_2
);

  wire and_1_out, and_2_out, and_3_out, and_4_out, and_5_out, and_6_out, and_7_out, and_8_out, and_9_out,
       reg_a0_write, reg_ra_write, reg_s0_write, reg_s1_write, reg_sp_write, reg_t0_write, reg_t1_write,
       reg_t2_write;
  wire [31:0] multiplexer_1_out, multiplexer_2_out, multiplexer_3_out, multiplexer_4_out, multiplexer_5_out,
       multiplexer_6_out, multiplexer_7_out, multiplexer_8_out, multiplexer_9_out;

  Multiplexer #(.width(32), .enable("false")) multiplexer_1 (
    .in0(out_16), .in1(Write_Data), .out(multiplexer_1_out), .sel(and_1_out));
  and and_1 (and_1_out, RegWEn, reg_ra_write);
  Multiplexer #(.width(32), .enable("false")) multiplexer_2 (
    .in0(ra), .in1(Write_Data), .out(multiplexer_2_out), .sel(and_2_out));
  and and_2 (and_2_out, RegWEn, reg_ra_write);
  Multiplexer #(.width(32), .enable("false")) multiplexer_3 (
    .in0(sp), .in1(Write_Data), .out(multiplexer_3_out), .sel(and_3_out));
  and and_3 (and_3_out, RegWEn, reg_sp_write);
  Multiplexer #(.width(32), .enable("false")) multiplexer_4 (
    .in0(t0), .in1(Write_Data), .out(multiplexer_4_out), .sel(and_4_out));
  and and_4 (and_4_out, RegWEn, reg_t0_write);
  Multiplexer #(.width(32), .enable("false")) multiplexer_5 (
    .in0(t1), .in1(Write_Data), .out(multiplexer_5_out), .sel(and_5_out));
  and and_5 (and_5_out, RegWEn, reg_t1_write);
  Multiplexer #(.width(32), .enable("false")) multiplexer_6 (
    .in0(t2), .in1(Write_Data), .out(multiplexer_6_out), .sel(and_6_out));
  and and_6 (and_6_out, RegWEn, reg_t2_write);
  Multiplexer #(.width(32), .enable("false")) multiplexer_7 (
    .in0(s0), .in1(Write_Data), .out(multiplexer_7_out), .sel(and_7_out));
  and and_7 (and_7_out, RegWEn, reg_s0_write);
  Multiplexer #(.width(32), .enable("false")) multiplexer_8 (
    .in0(s1), .in1(Write_Data), .out(multiplexer_8_out), .sel(and_8_out));
  and and_8 (and_8_out, RegWEn, reg_s1_write);
  Multiplexer #(.width(32), .enable("false")) multiplexer_9 (
    .in0(a0), .in1(Write_Data), .out(multiplexer_9_out), .sel(and_9_out));
  and and_9 (and_9_out, RegWEn, reg_a0_write);
  Register #(.width(32)) x0 (.D(multiplexer_1_out), .clk(clk), .Q(out_16));  // open: en, clr
  Register #(.width(32)) x1 (.D(multiplexer_2_out), .clk(clk), .Q(ra));  // open: en, clr
  Register #(.width(32)) x2 (.D(multiplexer_3_out), .clk(clk), .Q(sp));  // open: en, clr
  Register #(.width(32)) x5 (.D(multiplexer_4_out), .clk(clk), .Q(t0));  // open: en, clr
  Register #(.width(32)) x6 (.D(multiplexer_5_out), .clk(clk), .Q(t1));  // open: en, clr
  Register #(.width(32)) x7 (.D(multiplexer_6_out), .clk(clk), .Q(t2));  // open: en, clr
  Register #(.width(32)) x8 (.D(multiplexer_7_out), .clk(clk), .Q(s0));  // open: en, clr
  Register #(.width(32)) x9 (.D(multiplexer_8_out), .clk(clk), .Q(s1));  // open: en, clr
  Register #(.width(32)) x10 (.D(multiplexer_9_out), .clk(clk), .Q(a0));  // open: en, clr
  Demultiplexer #(.select(5), .enable("false")) demultiplexer_1 (
    .out1(reg_ra_write), .out2(reg_sp_write), .out5(reg_t0_write), .out6(reg_t1_write), .out7(reg_t2_write),
    .out8(reg_s0_write), .out9(reg_s1_write), .out10(reg_a0_write), .in(1'b1), .sel(rd));  // open: out0, out3, out4, out11, out12, out13, out14, out15, out16, out17, out18, out19, out20, out21, out22, out23, out24, out25, out26, out27, out28, out29, out30, out31
  Multiplexer #(.select(5), .width(32), .enable("false")) multiplexer_10 (
    .in0({32{1'b0}}), .in1(ra), .in2(sp), .in3({32{1'b0}}), .in4({32{1'b0}}), .in5(t0), .in6(t1), .in7(t2),
    .in8(s0), .in9(s1), .in10(a0), .in11({32{1'b0}}), .in12({32{1'b0}}), .in13({32{1'b0}}),
    .in14({32{1'b0}}), .in15({32{1'b0}}), .in16({32{1'b0}}), .in17({32{1'b0}}), .in18({32{1'b0}}),
    .in19({32{1'b0}}), .in20({32{1'b0}}), .in21({32{1'b0}}), .in22({32{1'b0}}), .in23({32{1'b0}}),
    .in24({32{1'b0}}), .in25({32{1'b0}}), .in26({32{1'b0}}), .in27({32{1'b0}}), .in28({32{1'b0}}),
    .in29({32{1'b0}}), .in30({32{1'b0}}), .in31({32{1'b0}}), .out(Read_Data_1), .sel(rs1));
  Multiplexer #(.select(5), .width(32), .enable("false")) multiplexer_11 (
    .in0({32{1'b0}}), .in1(ra), .in2(sp), .in3({32{1'b0}}), .in4({32{1'b0}}), .in5(t0), .in6(t1), .in7(t2),
    .in8(s0), .in9(s1), .in10(a0), .in11({32{1'b0}}), .in12({32{1'b0}}), .in13({32{1'b0}}),
    .in14({32{1'b0}}), .in15({32{1'b0}}), .in16({32{1'b0}}), .in17({32{1'b0}}), .in18({32{1'b0}}),
    .in19({32{1'b0}}), .in20({32{1'b0}}), .in21({32{1'b0}}), .in22({32{1'b0}}), .in23({32{1'b0}}),
    .in24({32{1'b0}}), .in25({32{1'b0}}), .in26({32{1'b0}}), .in27({32{1'b0}}), .in28({32{1'b0}}),
    .in29({32{1'b0}}), .in30({32{1'b0}}), .in31({32{1'b0}}), .out(Read_Data_2), .sel(rs2));

  // Other names for the same wires on the sheet: read_data1[31:0] = Read_Data_1; read_data2[31:0] = Read_Data_2;
  //   read_reg1[4:0] = rs1; read_reg2[4:0] = rs2; write_en = RegWEn; write_reg[4:0] = rd

  // Notes on the sheet:
  //   INPUTS to your circuit
  //   DON'T CHANGE THE LOCATIONS OF THE INPUTS AND OUTPUTS!
  //   These are DEBUG/TEST outputs from your circuit.
  //   OUTPUTS from your circuit
endmodule
